// Logisim project Signal.circ as structural Verilog
module SR_Latch (
  input  R,
  input  S,
  output Q,
  output Not_Q
);

  nor nor_1 (Q, R, Not_Q);
  nor nor_2 (Not_Q, Q, S);
endmodule

module D_Latch (
  input  D,
  input  WE,
  input  reset,
  output Q,
  output Not_Q
);

  wire and_1_out, and_2_out, and_3_out, not_1_out, not_2_out, or_1_out;

  not not_1 (not_1_out, D);
  and and_1 (and_1_out, not_1_out, WE);
  and and_2 (and_2_out, WE, D);
  or or_1 (or_1_out, and_1_out, reset);
  not not_2 (not_2_out, reset);
  and and_3 (and_3_out, not_2_out, and_2_out);
  SR_Latch sr_latch_1 (.R(or_1_out), .S(and_3_out), .Q(Q), .Not_Q(Not_Q));
endmodule
