// Logisim project sCPU.circ as structural Verilog: 2 circuits, main circuit main
module main (
);

  wire and_1_out, and_2_out, and_3_out, and_4_out, clock_1_out, clock_2_out, clock_3_out, decoder_1_out0,
       decoder_1_out1, decoder_1_out2, decoder_1_out3, op_add, op_bner0, op_li, rd_can_write, reset;
  wire [1:0] op_code, rd, rs1, rs2;
  wire [3:0] addr, imm;
  wire [7:0] CMD, PC;

  Clock clock_1 (.out(clock_1_out));
  Counter counter_1 (.clr(reset), .clk(clock_1_out), .Q(PC));  // open: load, up, count, D, carry
  Button button_1 (.out(reset));
  Decoder #(.select(2)) decoder_1 (
    .out0(decoder_1_out0), .out1(decoder_1_out1), .out2(decoder_1_out2), .out3(decoder_1_out3), .sel(rd));  // open: en
  OP_Seperator op_seperator_1 (.op(CMD), .op_code(op_code), .rd(rd), .addr(addr), .rs1(rs1), .imm(imm), .rs2(rs2));
  Clock clock_2 (.out(clock_2_out));
  // Probe on PC
  Clock clock_3 (.out(clock_3_out));
  RAM ram_1 (.addr(PC), .oe(1'b1), .clk(clock_3_out), .dout(CMD));  // open: we, din
  Decoder #(.select(2)) decoder_2 (.out0(op_add), .out2(op_li), .out3(op_bner0), .sel(op_code));  // open: out1, en
  or or_1 (rd_can_write, op_add, op_li);
  Register #(.width(4)) R0 (.D(imm), .en(and_1_out), .clk(clock_2_out), .clr(reset));  // open: Q
  and and_1 (and_1_out, decoder_1_out0, rd_can_write);
  Register #(.width(4)) R1 (.D(imm), .en(and_2_out), .clk(clock_2_out), .clr(reset));  // open: Q
  and and_2 (and_2_out, decoder_1_out1, rd_can_write);
  Register #(.width(4)) R2 (.D(imm), .en(and_3_out), .clk(clock_2_out), .clr(reset));  // open: Q
  and and_3 (and_3_out, decoder_1_out2, rd_can_write);
  Register #(.width(4)) R3 (.D(imm), .en(and_4_out), .clk(clock_2_out), .clr(reset));  // open: Q
  and and_4 (and_4_out, decoder_1_out3, rd_can_write);
  // Probe on CMD

  // Other names for the same wires on the sheet: write_data[3:0] = imm
endmodule

module OP_Seperator (
  input  [7:0] op,
  output [1:0] op_code,
  output [1:0] rd,
  output [3:0] addr,
  output [1:0] rs1,
  output [3:0] imm,
  output [1:0] rs2
);


  assign addr = op[5:2];
  assign imm = op[3:0];
  assign op_code = op[7:6];
  assign rd = op[5:4];
  assign rs1 = op[3:2];
  assign rs2 = op[1:0];
endmodule
