// Logisim project minirv.circ as structural Verilog: 1 circuit, main circuit main
module main (
);

  wire clock_1_out, clock_2_out, clock_3_out, comparator_1_eq, comparator_2_eq, comparator_3_eq,
       comparator_4_eq, comparator_5_eq, comparator_6_eq, comparator_7_eq, comparator_9_eq, comparator_10_eq,
       comparator_11_eq, comparator_12_eq, comparator_13_eq, comparator_14_eq, comparator_15_eq,
       comparator_16_eq, decoder_1_out0, decoder_1_out1, decoder_1_out2, decoder_1_out3, decoder_1_out4,
       decoder_1_out5, decoder_1_out6, decoder_1_out7, decoder_1_out8, decoder_1_out9, decoder_1_out10,
       decoder_1_out11, decoder_1_out12, decoder_1_out13, decoder_1_out14, decoder_1_out15, is_add, is_addi,
       is_jalr, is_lbu, is_lui, is_lw, is_sb, is_sw, reset;
  wire [2:0] funct3;
  wire [3:0] rd_selector, rs1_selector, rs2_selector;
  wire [4:0] I_Type_imm;
  wire [6:0] funct7, opcode;
  wire [15:0] bit_extender_1_out;
  wire [19:7] RAM_data;
  wire [31:0] adder_1_out, adder_2_out, adder_3_out, adder_4_out, adder_5_out, and_1_out,
       bit_extender_10_out, bit_extender_11_out, bit_extender_12_out, bit_extender_13_out, multiplexer_1_out,
       new_PC_data, new_RAM_data, PC_data, rs1_data, rs2_data, shifter_1_out, shifter_2_out, shifter_3_out,
       shifter_4_out, target_addr, write_data, x0_zero_q, x1_ra_q, x2_sp_q, x3_gp_q, x4_tp_q, x5_t0_q,
       x6_t1_q, x7_t2_q, x8_s0_fp_q, x9_s1_q, x10_a0_q, x11_a1_q, x12_a2_q, x13_a3_q, x14_a4_q, x15_a5_q;

  Clock clock_1 (.out(clock_1_out));
  Clock clock_2 (.out(clock_2_out));
  Counter #(.max('hffffffff), .width(32)) PC_counter (
    .clr(reset), .load(is_jalr), .up(1'b1), .clk(clock_1_out), .D(new_PC_data), .Q(PC_data));  // open: count, carry
  // Probe on write_data
  // NoConnect on decoder_1_out0
  Decoder #(.select(4)) decoder_1 (
    .out0(decoder_1_out0), .out1(decoder_1_out1), .out2(decoder_1_out2), .out3(decoder_1_out3),
    .out4(decoder_1_out4), .out5(decoder_1_out5), .out6(decoder_1_out6), .out7(decoder_1_out7),
    .out8(decoder_1_out8), .out9(decoder_1_out9), .out10(decoder_1_out10), .out11(decoder_1_out11),
    .out12(decoder_1_out12), .out13(decoder_1_out13), .out14(decoder_1_out14), .out15(decoder_1_out15),
    .sel(rd_selector));  // open: en
  // Probe on write_data
  Register #(.width(32)) x0_zero (.D(write_data), .en(1'b0), .clk(clock_2_out), .Q(x0_zero_q), .clr(1'b1));
  Register #(.width(32)) x8_s0_fp (.D(write_data), .en(decoder_1_out8), .clk(clock_2_out), .Q(x8_s0_fp_q), .clr(reset));
  Register #(.width(32)) x1_ra (.D(write_data), .en(decoder_1_out1), .clk(clock_2_out), .Q(x1_ra_q), .clr(reset));
  Register #(.width(32)) x9_s1 (.D(write_data), .en(decoder_1_out9), .clk(clock_2_out), .Q(x9_s1_q), .clr(reset));
  // OR_Gate or_1 has open pins: in0=is_lw, in1=is_lbu, in2=is_sw, in3=is_sb, out=open
  // OR_Gate or_2 has open pins: in0=is_sw, in1=is_sb, out=open
  Register #(.width(32)) x2_sp (.D(write_data), .en(decoder_1_out2), .clk(clock_2_out), .Q(x2_sp_q), .clr(reset));
  Register #(.width(32)) x10_a0 (.D(write_data), .en(decoder_1_out10), .clk(clock_2_out), .Q(x10_a0_q), .clr(reset));
  Multiplexer #(.width(32)) multiplexer_1 (.in0(PC_data), .in1(target_addr), .out(multiplexer_1_out), .sel(1'b0));
  Clock clock_3 (.out(clock_3_out));
  Register #(.width(32)) x3_gp (.D(write_data), .en(decoder_1_out3), .clk(clock_2_out), .Q(x3_gp_q), .clr(reset));
  Register #(.width(32)) x11_a1 (.D(write_data), .en(decoder_1_out11), .clk(clock_2_out), .Q(x11_a1_q), .clr(reset));
  // Probe on multiplexer_1_out
  RAM #(.addrWidth(16), .asyncread("true"), .byteenables("byteEnables"), .dataWidth(32), .\type ("nonvolatile")) ram_1 (
    .addr(bit_extender_1_out), .we(1'b0), .oe(1'b1), .clk(clock_3_out), .din(new_RAM_data),
    .dout({funct7, I_Type_imm, RAM_data[19:15], funct3, RAM_data[11:7], opcode}), .be3(1'b0), .be2(1'b0),
    .be1(1'b0), .be0(1'b0));
  Bit_Extender #(.in_width(32), .\type ("zero")) bit_extender_1 (.in(multiplexer_1_out), .out(bit_extender_1_out));
  Button reset_button (.out(reset));
  Register #(.width(32)) x4_tp (.D(write_data), .en(decoder_1_out4), .clk(clock_2_out), .Q(x4_tp_q), .clr(reset));
  Register #(.width(32)) x12_a2 (.D(write_data), .en(decoder_1_out12), .clk(clock_2_out), .Q(x12_a2_q), .clr(reset));
  Register #(.width(32)) x5_t0 (.D(write_data), .en(decoder_1_out5), .clk(clock_2_out), .Q(x5_t0_q), .clr(reset));
  Register #(.width(32)) x13_a3 (.D(write_data), .en(decoder_1_out13), .clk(clock_2_out), .Q(x13_a3_q), .clr(reset));
  Register #(.width(32)) x6_t1 (.D(write_data), .en(decoder_1_out6), .clk(clock_2_out), .Q(x6_t1_q), .clr(reset));
  Register #(.width(32)) x14_a4 (.D(write_data), .en(decoder_1_out14), .clk(clock_2_out), .Q(x14_a4_q), .clr(reset));
  // Probe on {funct7, I_Type_imm, RAM_data[19:15], funct3, RAM_data[11:7], opcode}
  Register #(.width(32)) x7_t2 (.D(write_data), .en(decoder_1_out7), .clk(clock_2_out), .Q(x7_t2_q), .clr(reset));
  Register #(.width(32)) x15_a5 (.D(write_data), .en(decoder_1_out15), .clk(clock_2_out), .Q(x15_a5_q), .clr(reset));
  Multiplexer #(.select(4), .width(32)) multiplexer_2 (
    .in0(x0_zero_q), .in1(x1_ra_q), .in2(x2_sp_q), .in3(x3_gp_q), .in4(x4_tp_q), .in5(x5_t0_q),
    .in6(x6_t1_q), .in7(x7_t2_q), .in8(x8_s0_fp_q), .in9(x9_s1_q), .in10(x10_a0_q), .in11(x11_a1_q),
    .in12(x12_a2_q), .in13(x13_a3_q), .in14(x14_a4_q), .in15(x15_a5_q), .out(rs1_data), .sel(rs1_selector));
  Multiplexer #(.select(4), .width(32)) multiplexer_3 (
    .in0(x0_zero_q), .in1(x1_ra_q), .in2(x2_sp_q), .in3(x3_gp_q), .in4(x4_tp_q), .in5(x5_t0_q),
    .in6(x6_t1_q), .in7(x7_t2_q), .in8(x8_s0_fp_q), .in9(x9_s1_q), .in10(x10_a0_q), .in11(x11_a1_q),
    .in12(x12_a2_q), .in13(x13_a3_q), .in14(x14_a4_q), .in15(x15_a5_q), .out(rs2_data), .sel(rs2_selector));
  Bit_Extender #(.in_width(5), .out_width(4), .\type ("zero")) bit_extender_2 (.in(RAM_data[11:7]), .out(rd_selector));
  Bit_Extender #(.in_width(5), .out_width(4), .\type ("zero")) bit_extender_3 (
    .in(RAM_data[19:15]), .out(rs1_selector));
  Bit_Extender #(.in_width(5), .out_width(4), .\type ("zero")) bit_extender_4 (.in(RAM_data[11:7]), .out(rd_selector));
  Bit_Extender #(.in_width(5), .out_width(4), .\type ("zero")) bit_extender_5 (
    .in(RAM_data[19:15]), .out(rs1_selector));
  Bit_Extender #(.in_width(5), .out_width(4), .\type ("zero")) bit_extender_6 (.in(I_Type_imm), .out(rs2_selector));
  Bit_Extender #(.in_width(5), .out_width(4), .\type ("zero")) bit_extender_7 (.in(RAM_data[11:7]), .out(rd_selector));
  Bit_Extender #(.in_width(5), .out_width(4), .\type ("zero")) bit_extender_8 (
    .in(RAM_data[19:15]), .out(rs1_selector));
  Bit_Extender #(.in_width(5), .out_width(4), .\type ("zero")) bit_extender_9 (.in(I_Type_imm), .out(rs2_selector));
  // Probe on opcode
  // Probe on funct3
  // Probe on funct7
  // Probe on rd_selector
  // Probe on rs1_selector
  // Probe on rs2_selector
  // Probe on {funct7, I_Type_imm}
  // Probe on {funct7, I_Type_imm, RAM_data[19:15], funct3}
  // Probe on {funct7, RAM_data[11:7]}
  assign bit_extender_10_out = {{20{funct7[6]}}, {funct7, I_Type_imm}};  // Bit_Extender bit_extender_10
  assign bit_extender_11_out = {{20{funct7[6]}}, {funct7, I_Type_imm}};  // Bit_Extender bit_extender_11
  // Probe on adder_1_out
  Adder #(.width(32)) adder_1 (.a(rs1_data), .b(rs2_data), .out(adder_1_out));  // open: cin, cout
  assign bit_extender_12_out = {{12{funct7[6]}}, {funct7, I_Type_imm, RAM_data[19:15], funct3}};  // Bit_Extender bit_extender_12
  assign bit_extender_13_out = {{20{funct7[6]}}, {funct7, I_Type_imm}};  // Bit_Extender bit_extender_13
  Adder #(.width(32)) adder_2 (.a(bit_extender_10_out), .b(rs1_data), .out(adder_2_out));  // open: cin, cout
  Adder #(.width(32)) adder_3 (.a(bit_extender_11_out), .b(rs1_data), .out(adder_3_out));  // open: cin, cout
  assign write_data = is_add ? adder_1_out : 32'bz;  // Controlled_Buffer controlled_buffer_1
  // Probe on shifter_1_out
  Shifter #(.width(32)) shifter_1 (.in(bit_extender_12_out), .\dist (5'b01100), .out(shifter_1_out));
  Adder #(.width(32)) adder_4 (.a(bit_extender_13_out), .b(rs1_data), .out(adder_4_out));  // open: cin, cout
  // Probe on adder_2_out
  // Probe on and_1_out
  assign and_1_out = 32'hfffffffe & adder_3_out;  // AND_Gate and_1, 32 bits wide
  Adder #(.width(32)) adder_5 (.a(PC_data), .b(32'h1), .out(adder_5_out));  // open: cin, cout
  assign write_data = is_lui ? shifter_1_out : 32'bz;  // Controlled_Buffer controlled_buffer_2
  assign write_data = is_addi ? adder_2_out : 32'bz;  // Controlled_Buffer controlled_buffer_3
  Shifter #(.shift("lr"), .width(32)) shifter_2 (.in(and_1_out), .\dist (5'b00010), .out(shifter_2_out));
  Shifter #(.width(32)) shifter_3 (.in(adder_5_out), .\dist (5'b00010), .out(shifter_3_out));
  assign target_addr = is_lw ? shifter_4_out : 32'bz;  // Controlled_Buffer controlled_buffer_4
  Shifter #(.shift("lr"), .width(32)) shifter_4 (.in(adder_4_out), .\dist (5'b00010), .out(shifter_4_out));
  Comparator #(.mode("unsigned"), .width(7)) comparator_1 (
    .a(7'b0010011), .b(opcode), .eq(comparator_1_eq));  // open: gt, lt
  Comparator #(.mode("unsigned"), .width(3)) comparator_2 (
    .a(3'b000), .b(funct3), .eq(comparator_2_eq));  // open: gt, lt
  Comparator #(.mode("unsigned"), .width(7)) comparator_3 (
    .a(7'b1100111), .b(opcode), .eq(comparator_3_eq));  // open: gt, lt
  Comparator #(.mode("unsigned"), .width(3)) comparator_4 (
    .a(3'b000), .b(funct3), .eq(comparator_4_eq));  // open: gt, lt
  Comparator #(.mode("unsigned"), .width(7)) comparator_5 (
    .a(7'b0110011), .b(opcode), .eq(comparator_5_eq));  // open: gt, lt
  Comparator #(.mode("unsigned"), .width(3)) comparator_6 (
    .a(3'b000), .b(funct3), .eq(comparator_6_eq));  // open: gt, lt
  Comparator #(.mode("unsigned"), .width(7)) comparator_7 (
    .a({7{1'b0}}), .b(funct7), .eq(comparator_7_eq));  // open: gt, lt
  Comparator #(.mode("unsigned"), .width(7)) comparator_8 (.a(7'b0110111), .b(opcode), .eq(is_lui));  // open: gt, lt
  Comparator #(.mode("unsigned"), .width(7)) comparator_9 (
    .a(7'b0000011), .b(opcode), .eq(comparator_9_eq));  // open: gt, lt
  Comparator #(.mode("unsigned"), .width(3)) comparator_10 (
    .a(3'b010), .b(funct3), .eq(comparator_10_eq));  // open: gt, lt
  Comparator #(.mode("unsigned"), .width(7)) comparator_11 (
    .a(7'b0000011), .b(opcode), .eq(comparator_11_eq));  // open: gt, lt
  Comparator #(.mode("unsigned"), .width(3)) comparator_12 (
    .a(3'b100), .b(funct3), .eq(comparator_12_eq));  // open: gt, lt
  Comparator #(.mode("unsigned"), .width(7)) comparator_13 (
    .a(7'b0100011), .b(opcode), .eq(comparator_13_eq));  // open: gt, lt
  Comparator #(.mode("unsigned"), .width(3)) comparator_14 (
    .a(3'b010), .b(funct3), .eq(comparator_14_eq));  // open: gt, lt
  Comparator #(.mode("unsigned"), .width(7)) comparator_15 (
    .a(7'b0100011), .b(opcode), .eq(comparator_15_eq));  // open: gt, lt
  Comparator #(.mode("unsigned"), .width(3)) comparator_16 (
    .a(3'b000), .b(funct3), .eq(comparator_16_eq));  // open: gt, lt
  assign new_PC_data = is_jalr ? shifter_2_out : 32'bz;  // Controlled_Buffer controlled_buffer_5
  assign write_data = is_jalr ? shifter_3_out : 32'bz;  // Controlled_Buffer controlled_buffer_6
  and and_2 (is_addi, comparator_1_eq, comparator_2_eq);
  and and_3 (is_jalr, comparator_3_eq, comparator_4_eq);
  and and_4 (is_add, comparator_5_eq, comparator_6_eq, comparator_7_eq);
  and and_5 (is_lw, comparator_9_eq, comparator_10_eq);
  and and_6 (is_lbu, comparator_11_eq, comparator_12_eq);
  and and_7 (is_sw, comparator_13_eq, comparator_14_eq);
  and and_8 (is_sb, comparator_15_eq, comparator_16_eq);

  // Other names for the same wires on the sheet: RAM_data (some bits) = {funct7, I_Type_imm, funct3, opcode};
  //   U_Type_imm[19:0] = {funct7, I_Type_imm, RAM_data[19:15], funct3}; S_Type_imm[11:0] = {funct7, RAM_data[11:7]};
  //   I_Type_imm[11:5] = funct7; write_PC = is_jalr

  // Notes on the sheet:
  //   I-Type Parse
  //   R-Type Parse
  //   U-Type Parse
  //   S-Type Parse
  //   Operation Parser
  //   Operation Options
  //   LUI
  //   LW
  //   ADDI
  //   JALR
  //   rd 中存储 PC+1
  //   ADD
  //   Operation Judement
endmodule
